// Logisim project MLP_circit.circ as structural Verilog: 7 circuits, main circuit main
module main (
  input  in_1,
  input  [7:0] in_2
);

  wire clear, clk, controlled_buffer_1_out, finish, start, start_out;
  wire [3:0] result, rgb_video_1_p4, rgb_video_1_p5;
  wire [7:0] counter_1_q, multiplexer_1_out;
  wire [31:0] multiplexer_2_out;

  Button u_clear (.out(clear));
  Counter counter_1 (
    .clr(in_1), .clk(controlled_buffer_1_out), .D(in_2), .Q(counter_1_q));  // open: load, up, count, carry
  assign controlled_buffer_1_out = clear ? clk : 1'bz;  // Controlled_Buffer controlled_buffer_1
  Clock clock_1 (.out(clk));
  // RGB_Video #(.cursor("No Cursor"), .height(16), .scale(8), .width(16)) rgb_video_1: pin names not known; wires that end beside it: clear, clk, 1'b1, rgb_video_1_p4, rgb_video_1_p5
  Joystick joystick_1 (.x(rgb_video_1_p4), .y(rgb_video_1_p5));
  LED led_1 (.in(finish));
  Hex_Digit_Display hex_digit_display_1 (.value(result));  // open: dp
  Multiplexer #(.width(8)) multiplexer_1 (
    .in0({rgb_video_1_p5, rgb_video_1_p4}), .in1(counter_1_q), .out(multiplexer_1_out), .sel(clear));
  Multiplexer #(.width(32)) multiplexer_2 (.in0(32'h3f800000), .in1({32{1'b0}}), .out(multiplexer_2_out), .sel(clear));
  Button u_start (.out(start_out));
  LED led_2 (.in(start));
  D_Flip_Flop d_ff_1 (.D(start_out), .clk(start_out), .Q(start), .reset(clear));  // open: Qn, preset
  MLP mlp_1 (
    .clk(clk), .clear(clear), .start(start), .address(multiplexer_1_out), .inputValue(multiplexer_2_out),
    .finish(finish), .result(result));
endmodule

module ReLU (
  input  [31:0] value,
  output [31:0] result
);

  wire fpcomparator_1_p3;

  // FPComparator fpcomparator_1: pin names not known; wires that end beside it: value, {32{1'b0}}, fpcomparator_1_p3
  Multiplexer #(.width(32)) multiplexer_1 (.in0(value), .in1({32{1'b0}}), .out(result), .sel(fpcomparator_1_p3));
endmodule

module MAC (
  input  [31:0] value,
  input  [31:0] bias,
  input  [31:0] weight,
  input  start,
  input  clk,
  input  reset,
  output [31:0] result
);

  wire [31:0] fpadder_1_out, fpmultiplier_1_out, sum_q;

  FPMultiplier fpmultiplier_1 (.a(value), .b(weight), .out(fpmultiplier_1_out));
  FPAdder fpadder_1 (.a(fpmultiplier_1_out), .b(sum_q), .out(fpadder_1_out));
  Register #(.width(32)) sum (.D(fpadder_1_out), .en(start), .clk(clk), .Q(sum_q), .clr(reset));
  FPAdder fpadder_2 (.a(bias), .b(sum_q), .out(result));
endmodule

module MLP (
  input  clk,
  input  clear,
  input  start,
  input  [7:0] address,
  input  [31:0] inputValue,
  output finish,
  output [3:0] result
);

  wire hiddenlayer_1_nextnode, hiddenlayer_1_start, inputlayer_1_reset, inputlayer_1_start2, node_full1,
       node_full2;
  wire [6:0] hiddenlayer_1_idx2;
  wire [7:0] inputlayer_1_idx1;
  wire [31:0] hiddenlayer_1_outputvalue, inputlayer_1_outputvalue;

  InputLayer inputlayer_1 (
    .clk(clk), .start(start), .clear(clear), .node_full1(node_full1), .address(address),
    .inputValue(inputValue), .start2(inputlayer_1_start2), .idx1(inputlayer_1_idx1),
    .reset(inputlayer_1_reset), .outputValue(inputlayer_1_outputvalue));
  HiddenLayer hiddenlayer_1 (
    .clk(clk), .clear(clear), .idx1(inputlayer_1_idx1), .node_full2(node_full2), .reset(inputlayer_1_reset),
    .inputValue(inputlayer_1_outputvalue), .start2(inputlayer_1_start2), .start(hiddenlayer_1_start),
    .nextNode(hiddenlayer_1_nextnode), .idx2(hiddenlayer_1_idx2), .outputValue(hiddenlayer_1_outputvalue),
    .node_full1(node_full1));
  OutputLayer outputlayer_1 (
    .clk(clk), .reset(hiddenlayer_1_nextnode), .clear(clear), .idx2(hiddenlayer_1_idx2),
    .inputValue(hiddenlayer_1_outputvalue), .start(hiddenlayer_1_start), .node_full2(node_full2),
    .finish(finish), .result(result));
endmodule

module InputLayer (
  input  clk,
  input  start,
  input  clear,
  input  node_full1,
  input  [7:0] address,
  input  [31:0] inputValue,
  output start2,
  output [7:0] idx1,
  output reset,
  output [31:0] outputValue
);

  wire controlled_buffer_1_out, not_1_out;
  wire [7:0] multiplexer_1_out, undriven;

  xor xor_1 (start2, start, node_full1);
  Multiplexer #(.width(8)) multiplexer_1 (.in0(address), .in1(idx1), .out(multiplexer_1_out), .sel(start));
  Counter counter_1 (
    .clr(clear), .clk(controlled_buffer_1_out), .D(undriven), .carry(reset), .Q(idx1));  // open: load, up, count
  assign controlled_buffer_1_out = start2 ? clk : 1'bz;  // Controlled_Buffer controlled_buffer_1
  RAM #(.dataWidth(32)) InputLayer (
    .addr(multiplexer_1_out), .we(not_1_out), .oe(start), .clk(clk), .din(inputValue), .dout(outputValue));
  not not_1 (not_1_out, start);
endmodule

module HiddenLayer (
  input  clk,
  input  clear,
  input  [7:0] idx1,
  input  node_full2,
  input  reset,
  input  [31:0] inputValue,
  input  start2,
  output start,
  output nextNode,
  output [6:0] idx2,
  output [31:0] outputValue,
  output node_full1
);

  wire controlled_buffer_1_out, not_1_out, not_2_out;
  wire [6:0] multiplexer_1_out, node1, undriven;
  wire [14:0] adder_1_out, bit_extender_1_out, bit_extender_2_out, shifter_1_out;
  wire [31:0] FC1_bias_data, FC1_weight_data, mac_1_result, relu_1_result;

  assign bit_extender_1_out = {{8{1'b0}}, node1};  // Bit_Extender bit_extender_1
  Shifter #(.width(15)) shifter_1 (.in(bit_extender_1_out), .\dist (4'b1000), .out(shifter_1_out));
  assign bit_extender_2_out = {{7{1'b0}}, idx1};  // Bit_Extender bit_extender_2
  Adder #(.width(15)) adder_1 (.a(bit_extender_2_out), .b(shifter_1_out), .out(adder_1_out));  // open: cin, cout
  ROM #(.addrWidth(15), .dataWidth(32)) FC1_weight (.addr(adder_1_out), .data(FC1_weight_data));
  Counter #(.max('h7f), .width(7)) counter_1 (
    .clr(clear), .count(not_1_out), .clk(reset), .D(undriven), .carry(node_full1), .Q(node1));  // open: load, up
  not not_1 (not_1_out, node_full1);
  ROM #(.addrWidth(7), .dataWidth(32)) FC1_bias (.addr(node1), .data(FC1_bias_data));
  Counter #(.max('h7f), .width(7)) counter_2 (
    .clr(clear), .clk(controlled_buffer_1_out), .carry(nextNode), .Q(idx2));  // open: load, up, count, D
  xor xor_1 (start, node_full1, node_full2);
  assign controlled_buffer_1_out = start ? clk : 1'bz;  // Controlled_Buffer controlled_buffer_1
  MAC mac_1 (
    .value(inputValue), .bias(FC1_bias_data), .weight(FC1_weight_data), .start(start2), .clk(clk),
    .reset(reset), .result(mac_1_result));
  ReLU relu_1 (.value(mac_1_result), .result(relu_1_result));
  RAM #(.addrWidth(7), .dataWidth(32)) HiddenLayer (
    .addr(multiplexer_1_out), .we(not_2_out), .oe(node_full1), .clk(clk), .din(relu_1_result),
    .dout(outputValue));
  Multiplexer #(.width(7)) multiplexer_1 (.in0(node1), .in1(idx2), .out(multiplexer_1_out), .sel(node_full1));
  not not_2 (not_2_out, node_full1);

  // Notes on the sheet:
  //   contents of FC1_weight (hex, n*v repeats v):
  //   8002cb39 800a6f57 1581834 1bd7446 17ea880 e4799 62c34 ffb0 80194bf7 8018bab8 81a77a74 1d6433f
  //   8015b24e 12a3fe 79fe4 80127a1a 80dfe8a8 1084d3 b6ee0 6595 80076255 800e737e b6b0f64a 3a40f3c2
  //   b99f7aae 3d33405b bc0d3800 33c3f2af 2675abcc 39c1c3fd b101051c 81e905f4 80129522 10789b 19b868 827db
  //   3c17b3a9 bc1af7fc 3d229868 bd15a697 3dc0ddf9 3d454584 3b8b9de4 3d0540cf 3d9c88b8 3e252069 3da5b204
  //   7b381 f0232 18da94 800adcd1 bb434e9f bde979b5 bc57aed8 be548148 bddc10ac be2cff74 3e8e8653 bd2a6cac
  //   3d5e390e 3ed9fc36 3e73dd96 3bc639aa 3d53f47f 58a59 60d30 bd62b154 bda16f7d be8dbc25 be48377a
  //   3cfdb7af bd3331ec bebf310c 3ea2f5d0 be47328c 3d8f5d7a 3ac61912 3c28d1ea bd268c3e 3c9a4431 80067bbd
  //   81d9dce4 bc3d299e bdc7e919 bddc8ce3 bc977156 bdc21777 bd8700de be835069 3d2714f7 3bd36dc9 3d37267a
  //   3e80af14 bf0c8c5a bea0e132 37cfe3d7 49bed a3bae bbcb2646 be35d7fc be230372 be11699d bdfe3ff5
  //   bd8a6ea0 be9f2553 bc9a23d8 3e64b65e 3f0b8f49 be34fe81 bedd3652 bddf8b9a 3c53e86e 1939111 1654d1
  //   bd1b1365 bd4fac17 be8df8e8 3d987266 3e7ab224 3cb50bc0 3e17fc67 3ee394e0 3ebccd47 bdb041cf bea7ca94
  //   bea03170 bd82a1e3 3b7147db b71ff 80051d36 3b892545 3a70b0ec 3cafeb50 3ae0e24d be574e1e bbb259e8
  //   3e9f7608 3bdad1e1 be3e9aab befcfe19 bef4d269 3ce396a6 bd88a573 ba1f98ff 8a846 7d605 8012aacc
  //   bd26382b bde5d42c bd9aad7f 3e5036ba bea8dc96 3dcfc51d be9ed66d be436d36 3e3823dd be95ecbb 3dc6896c
  //   bd9aa821 3c798b23 80196b7b e1a2c 242b6b8b 3ba4646a 3bb2c44b 3dea377b 3da9d149 bd534656 3e5577ec
  //   bdf08370 3e4262bd 3d657bbf 3c33ac26 3c3f1839 bccc4060 3d8ae0ab 8ace0 80015719 bbf4cc7f 3dae42c4
  //   bdf9dc4c 3e40ad4d bdddf60c be131ceb bd8e3222 bc918250 be4b781b 3eb9c300 3e05b067 3da93dc6 bd88a398
  //   37897374 b654e 183247 bafd08bd bcce71c4 3d941d9e bde99954 bd089c27 bd9423ce 3e17c900 3db05799
  //   3e652624 3edea038 bdaa1c1e 3d8b784e 3d66f265 bae20ea4 150de0c b2c8b 987f4 bc81b733 bdacc521 3e014644
  //   be134c48 be00a927 be1dfa9f bd1671c9 bdcd57f4 3e9d5658 3e4be14d 3dca175d b84b8407 80091e1b 81d4d71f
  //   8004f0e8 2ff4b 25e31a0d 3d388079 3c2b034f bd5fd950 3d9aa2d8 be30e96d bd519130 be4c645f be4d4004
  //   bd2d2cc1 3cee57fe bc12e77e 81c9c861 bf82f 19c59b2 f9130 8010606c 2a0f1 9aa39 2dbad72c ba3e7e8c
  //   bd6bae3b bd36cb16 bce67186 bb608346 b2b4d270 809eca68 80019f52 8005ba39 8000c25e 1293c44 b320f
  //   801292da 128c92 34ace 800d1865 80151aca 800ec9b5 c91d2 198f7e4 13811 80007c0b 8007596c 17990f ce6e68
  //   355dd c3402 3a305 81bd13c6 17ad68 3b1780c9 b302d703 bbc2b43a bb8c4873 bbe5bb80 3ccb65bc 2c335670
  //   af38e942 80049235 80073472 ab4ff 81d34efc 820aa009 11c0c1 bd0e3 39a3c9ac 3bf02a2a bc401790 3e39bff1
  //   be49cd37 3c93de46 3e3da9fe bd03dd0d bdc3ed63 3df32bf3 3d88091d 8005def4 1c5600b 800eab90 81bd5f6e
  //   3a22dceb bd7e417c be54e57e bd5ee8e5 3e6af3f3 bd534062 bca536a2 bc90ca7e 3ebccc4a 3eddc3c1 3ecd396d
  //   3c41a26b 3ca921c9 19fd52 18b2d 8e189 3b9825a4 3c909f89 3d6b3675 3d9d8248 3e686932 3eb7b0a9 3eea87df
  //   3eeceedd be0383dc be835592 bee003fb be52dff7 3d22d612 8016f786 8006a9bb 1e36245b bd5bf2f6 be0d9692
  //   be907da4 bd54f58c be7d0bb4 beeaba96 bf20f566 bfa60a89 bf533ab5 bf0b1a0a bed5c263 be4274b0 2fb7895a
  //   15209e 132367 2cf85914 bd8922a8 3dafe90a bc469d0d be3e5b0e 3da10e09 3cca516a 3e96c194 3e966eb1
  //   3e16a82c be41d0ec bd88d54b bdd4f26e ba11c645 49549 114952 3c917292 3d1e8b82 be1f4c04 bc2d88ad
  //   be6a3fa7 3d89ff42 3b918d62 3d62dd56 3eef1f9a bd62b457 3e3bf2c4 bd06ce9e 3d1b7a8a bd3c11e0 801285ff
  //   8006f8ed 8011186a bd89b8db bd7d3856 be357bcc 3dd2552b 3d306d2c 3e6e0603 3dfe8589 bc5643e3 3dfbdbcf
  //   3da0525f 3d29a5b6 bd28f82c 3c459cff 2ddfa 818e7f0e 17aa21 3cc43896 be418dfa bef15558 bdd37caf
  //   3e3252df bdd75627 bd4a6d8b 3ad20afb 3e409a7a 3e5c940c 3eb12300 3e3c8972 bccc07a2 80090a8a 1b4b61c
  //   3506ff4c bb0ab470 bd8c9fa5 be5bb212 be5474a0 be0d12de be3a427d bca55080 be9772c5 3cdc1f9b 3e71b7cb
  //   3e4396c1 3e653fc7 b983696a 80100a5c 8003b8b3 2209aabb 3e27348c 3d572e0d be32bf5e bd94cd3b bc331e91
  //   be49a67b 3d36b67b bbcffa59 bdbf6f7c 3e1e6adf 3e663c46 3e2aa5fe 3d06d9c5 18e646 81fc5fa0 395b1f12
  //   3d307264 bd2677b6 3cb72b4e 3e5bea59 3d75ca8b 3e0b41a9 bd487db9 3e6c9bc3 bd15abd4 3dab49a3 3dfcf9e5
  //   bdc2aa25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
  //   contents of FC1_bias (hex, n*v repeats v):
  //   391e5c6c 3def462d be0c10e4 bdc3c4ed 3c3f6c2e ba833a23 3ea01c58 3e7a6426 3e6ff607 3dabfd37 3eae8093
  //   3ed018e8 3e2fcbe3 3e701a0f bd4f92cd 3d1c502b 3c462cfe 3eed5fb2 3e34bebb 3e61779b 3e85ad55 3d9e1988
  //   3e9c3c39 3dccb590 3d92b4ae bd55d288 3e91e7cf 3df03f2a 3e70f7ee 3ec78504 3da572d9 3e64379a bd96aa7e
  //   3dd248f2 3dc7f088 bcd9a62d 3e3e1ce8 3ea36cb0 3e791c60 3a310d25 3e19a5d6 3f2355ac bcc0a4de 3da0baff
  //   3eb8aa19 3eb9fe51 3e6e5d11 be15d999 3b3ca332 3e09419d 3e494281 3db71f7f 3c855593 3dabe866 3eaddd09
  //   3c967834 bd4626f9 3dad9e61 3d95ff85 bd935efd 3f188371 bd9c9374 3e1db0d6 3cec2a17 3ee79005 3df05dc6
  //   3ee0f405 3f105c72 3e96133e 3ef4ee51 3e3f878e 3bda6e8f 3f0664f1 3e00554c 3eba9fff bd3ba0a9 3d85a5ec
  //   bda058ac bc5287fc 3e2735dc bc01b0dd bdb92739 baaae2cb bdde699e bdc1a9e7 3dd4871b bceca917 3e982d45
  //   3e335384 3e741dee 3e73eb41 3e903459 bd1aa846 3d2d188d 3ef9f392 3e9921c0 3dfd2cab 3d897b90 3c22b001
  //   3d4d5371 3e1f8103 3eaaeda3 3ec73129 3e2e0cce 3d758654 3c02dcd5 3e6a364d 3dab30da 3e1467f8 bd4899cd
  //   3e85ee9d 3db30612 3ee9af9f 3e7dfc85 3e1d741b ba8fcd1f 3e53d295 3e897988 3dedfef3 3d9a79f9 3e12b6d7
  //   ba5b6982 3ea0b75e 3d919e9a 3dd9234a 3d8471b1 be34b217 3dc4c856
endmodule

module OutputLayer (
  input  clk,
  input  reset,
  input  clear,
  input  [6:0] idx2,
  input  [31:0] inputValue,
  input  start,
  output node_full2,
  output finish,
  output [3:0] result
);

  wire comparator_3_eq, controlled_buffer_1_out, fpcomparator_1_p3, fpcomparator_2_p3, not_1_out, not_2_out,
       not_3_out;
  wire [3:0] address, multiplexer_1_out, multiplexer_3_out, node2, register_1_q, subtractor_1_out;
  wire [10:0] adder_1_out, bit_extender_1_out, bit_extender_2_out, shifter_1_out;
  wire [31:0] FC2_bias_data, FC2_weight_data, fpcomparator_2_p2, mac_1_result, multiplexer_2_out,
       multiplexer_5_out, OutputLayer_dout, register_2_q;

  not not_1 (not_1_out, node_full2);
  Counter #(.max('hf), .width(4)) counter_1 (
    .clr(clear), .count(not_1_out), .clk(reset), .Q(node2));  // open: load, up, D, carry
  ROM #(.addrWidth(4), .dataWidth(32)) FC2_bias (.addr(node2), .data(FC2_bias_data));
  assign bit_extender_1_out = {{7{1'b0}}, node2};  // Bit_Extender bit_extender_1
  Comparator #(.width(4)) comparator_1 (.a(4'b1011), .b(node2), .eq(node_full2));  // open: gt, lt
  assign bit_extender_2_out = {{4{1'b0}}, idx2};  // Bit_Extender bit_extender_2
  Adder #(.width(11)) adder_1 (.a(bit_extender_2_out), .b(shifter_1_out), .out(adder_1_out));  // open: cin, cout
  Shifter #(.width(11)) shifter_1 (.in(bit_extender_1_out), .\dist (4'b0111), .out(shifter_1_out));
  ROM #(.addrWidth(11), .dataWidth(32)) FC2_weight (.addr(adder_1_out), .data(FC2_weight_data));
  Counter #(.max('hf), .width(4)) counter_2 (
    .clr(clear), .count(not_2_out), .clk(controlled_buffer_1_out), .Q(address));  // open: load, up, D, carry
  Comparator #(.width(4)) comparator_2 (.a(4'b1010), .b(address), .eq(finish));  // open: gt, lt
  not not_2 (not_2_out, finish);
  assign controlled_buffer_1_out = node_full2 ? clk : 1'bz;  // Controlled_Buffer controlled_buffer_1
  MAC mac_1 (
    .value(inputValue), .bias(FC2_bias_data), .weight(FC2_weight_data), .start(start), .clk(clk),
    .reset(reset), .result(mac_1_result));
  RAM #(.addrWidth(4), .dataWidth(32)) OutputLayer (
    .addr(multiplexer_1_out), .we(not_3_out), .oe(node_full2), .clk(clk), .din(mac_1_result),
    .dout(OutputLayer_dout));
  Multiplexer #(.width(4)) multiplexer_1 (.in0(node2), .in1(address), .out(multiplexer_1_out), .sel(node_full2));
  not not_3 (not_3_out, node_full2);
  // FPComparator fpcomparator_1: pin names not known; wires that end beside it: {32{1'b0}}, OutputLayer_dout, fpcomparator_1_p3
  Multiplexer #(.width(32)) multiplexer_2 (
    .in0(OutputLayer_dout), .in1(32'hff800000), .out(multiplexer_2_out), .sel(fpcomparator_1_p3));
  // FPComparator fpcomparator_2: pin names not known; wires that end beside it: multiplexer_2_out, fpcomparator_2_p2, fpcomparator_2_p3
  Multiplexer #(.width(4)) multiplexer_3 (
    .in0(register_1_q), .in1(address), .out(multiplexer_3_out), .sel(fpcomparator_2_p3));
  Multiplexer #(.width(32)) multiplexer_4 (
    .in0(32'hff800000), .in1(register_2_q), .out(fpcomparator_2_p2), .sel(node_full2));
  Register #(.width(4)) register_1 (.D(multiplexer_3_out), .en(1'b1), .clk(clk), .Q(register_1_q), .clr(clear));
  Multiplexer #(.width(32)) multiplexer_5 (
    .in0(fpcomparator_2_p2), .in1(multiplexer_2_out), .out(multiplexer_5_out), .sel(fpcomparator_2_p3));
  Register #(.width(32)) register_2 (.D(multiplexer_5_out), .en(1'b1), .clk(clk), .Q(register_2_q), .clr(clear));
  Subtractor #(.width(4)) subtractor_1 (.a(register_1_q), .b(4'b0001), .out(subtractor_1_out));  // open: bin, bout
  Comparator #(.width(4)) comparator_3 (.a(subtractor_1_out), .b(4'b1111), .eq(comparator_3_eq));  // open: gt, lt
  Multiplexer #(.width(4)) multiplexer_6 (.in0(subtractor_1_out), .in1(4'b0000), .out(result), .sel(comparator_3_eq));

  // Notes on the sheet:
  //   contents of FC2_bias (hex, n*v repeats v):
  //   3d85a72a bd8963df 3ceeff53 bdc46215 be03d9d6 bd6569f2 bde10f67 3e000fdc be4d9fd1 3ec0533c
  //   contents of FC2_weight (hex, n*v repeats v):
  //   be5fa7b6 bf1d6278 bede7d07 3f0a8439 3ef298e6 3dc28707 3f171654 3e7a2b03 bf733d8f bed8b03e 3dfe55be
  //   3f15259f bdab0721 be30624d bf8fc5e1 3e0fdfc2 bf26bc89 3f0132ac bd95206d bf52d2d8 3e810849 bee929b6
  //   3ea46cc4 bf8a75a1 3e2a123a 3c1ab3a6 bf02034e 3db4005f bee9eea9 bf8fe84c 3f2c5104 bec6c0fd 3ea23709
  //   be83fac8 befe0b97 bea82b62 3e763343 bef87b01 bf0292ee 3e875997 be2a19b2 3e8dab76 bfa516ee 3e12117c
  //   3e9f4c5b bf384304 bd828ee9 3eea28cf 3e4d615a bddc5e55 be9607e0 3f16de09 bf244bca bfb70575 be94429f
  //   3f423677 be6e161b 3ede1b6f 3ea04a01 bf1e2d1d 3f259bc7 3ed06c1b bef1bf81 bf089e0a 3e5e7909 3e9f4695
  //   bf2f9db8 bed41d32 3dee9ba5 bf48a21e be9137e8 3f23f9c6 3c598f59 3ea89e03 3e970e69 3da91c7a 3ce6c9e6
  //   3ef78029 bee98fa7 3e67249f 3e609554 bdd93823 bf1059e0 be908ca0 3d609909 bf29c689 bf4da4bd bf0a2c2f
  //   be591c31 be905e30 3ec5b9fc bf0d03a9 3e9965ef bec49b74 bec1d243 bf2ab5cc beaf707e bf899c1f be787dd2
  //   bed3660e bf4a5448 3f8d1df7 3e2f5e66 3ea92822 3da1ecb0 beeb1dd9 beb5eeb5 3c457679 bef82209 3f198af6
  //   3ec8f3af 3e4d4d08 3c59ffa0 3d77237f bdc6f0e3 bef9b289 bf175aeb 3f1e9b23 3eefb3b3 3daa665d 3e8b7b70
  //   bf14454e 3e5b68b5 bf81a74e bee81e66 bf3583ae 3f08a0be 3eb9e83a bf74d3c3 3e8d816f bf843abe bee16879
  //   3e00ba3c 3db42e97 3e8c448b beee3e1d bf645c10 bf9604f3 3e89958a be0f5db9 3e7bbd76 bdcbbba6 3e026f5a
  //   bf4a70ea be8b9d7b bf041140 bd95c116 3e35692a 3dcba858 3e08dd92 bf43636d bf3e7972 bf1c8802 bedf42d3
  //   3eba1a7d 3f5ed917 3e22acd5 bf5c17dd bed1a0df 3ea90c78 be620905 3e81eff6 bf6c0f74 be94bdeb bf10297d
  //   bf4f341a 3c3b0cae be4aff5d 3f8ab946 3f04f083 3e9bac5e bf266ec2 3e70f379 bda9abac 3e467dbc bed854d5
  //   bece3016 beb1d5be 3e71618c 3edc09ce bdfa4343 befd9459 3f03ab60 be5db930 3ea41519 beff81c8 beaa03c0
  //   bec22b89 3f615f7f bf16a583 3f3dacc5 3e9a8ecb bcff55de bea7bbc6 3ee71a87 3f86d558 be22a815 3ee60a32
  //   bf61ee4e beb70588 bebb1356 bead9add bf55dbe4 bde52ced bf80b2b1 bf9b9a52 3e4191c2 3f95c68b be0c64f8
  //   3e8afc87 bf8dd95a bf01605b bf2ed727 3e922de2 bf21e2e2 be8a3630 3f31a6da bf6314b4 bf75ca21 3eb0e2bd
  //   bf19a937 bf535752 bf1a6d47 3eb8df6d beb1d138 3d869376 3f29947d 3e1aa891 be910fc5 bcb4ea0e bf5f22f5
  //   bcc5330b bedbcf24 bf0d47d7 3e97becd bd8cfe7b 3f5d65d6 bfa2d012 beb07200 3f55f176 3c90ad9f 3e3282fc
  //   3d7340fe bf376266 3ec28a43 bf27d940 3ea57fd8 bf16ef5a 3c3c151b bd1a1340 bddd82be bf18d9c1 3ee8dc2b
  //   3e8e4285 bd6a0613 3e0554c7 3d5d0a5b bd43505f bed0b174 3f186e2a bef68ba8 3e4fa439 bea2f204 be6d3393
  //   beda332f 3f1ef7f7 be3f0bb2 bbb1ca2a beb46370 be648c40 3e4f602d be3a8ea2 3e920785 bf083624 3f06a6ff
  //   3f666327 be865c8d 3e352f4a bf5188dc bf0ba5a8 be212bd5 3e941ce6 bf3eeb43 bf91540e bf47cfdd be51dd9f
  //   bf9e6534 3eb87c05 bee6bfd9 bf2a181f bf21e098 bf5582e1 bde8d510 3e77fc8a beae14bb 3f06c8e8 bea28eb2
  //   3ed330e6 bf14c530 3d0fdec1 3e03359e bf283a8d bf968014 3e764dea 3e8dfcf4 bea6aeac 3f6449b6 bd00691b
  //   3ef55bdb 3f298658 bebda5ad bf62c78b 3e80d1ac be8d7971 3ea6928c 3e84eb2a 3f1620a0 3ea29976 3eef2b17
  //   bd3f6881 3e7204dc bda8a941 3b88d037 bd5d861f 3f0e203e bf5f808a be16ab67 3d0cca80 3ea3a24d 3ec1d878
  //   3ec4a14c 3ed19257 bd13d22f 3f7b27b2 3e99bb44 bdd00dbc bce0f279 39f86e5e 3e9c7476 3e44f9a7 bdb8d6b4
  //   3d040db2 3f0b213e bf03e7a0 3ef9df51 bdb877c1 3f0ac0e8 3d8ba1d6 3eb7867c bf0b6e24 bf0077c8 beb8ada8
  //   3e9da20b 3f520680 3eb4686e bed64767 bf5f43ff babc2ee7 bf3f6eeb 3e92b613 3f03426d be5eea08 3f353e7a
  //   3e2b1dfd 3f372dda 3edfad8b bfa8b4e4 bc6c1eb5 bf4965a9 3d37b0a5 bd6794ff 3e8ef455 bf179cdd 3de82fe6
  //   3da42016 3e9b0447 bf2910cb 3ec5f1dc 3d832b28 3d932c7a 3f250915 bf3c3397 3e9af807 bf4bb8ac 3f544490
  //   3d166ea5 3d2936ff 3dd74aca bf9daf0a 3ee08206 bf03c3f7 3e46d6aa 3e9eda1f 3eaac215 bd90b3e8 3eab1848
  //   3f27858a 3eb7f057 3dc5af8b 3e89ec2a bf4fdf33 3efa7044 3e6cb2a4 befe8ad6 bf892750 3ecf82e6 3dcccf23
  //   3f33aea8 3d9653d1 3eca7bc4 3eaf152b bf6ed05c 3e3a4d92 bf2e8d53 beeaad50 3ec70952 bea8a78a bf22fe39
  //   3f098d7b 3e9e8646 bf0f9413 bed65244 bf1d690d bf531e03 3dd2df41 3eee723f 3d5604dd 3f12f7b2 bf4e384a
  //   3f8ed095 beed4264 3e134fb1 bee57e9e bf5a78c9 3bc9b44f 3cfb8dd4 3db3908e be15cbc6 bed971e1 3cd0859c
  //   3f2da391 bf1ae219 3e3638d3 3ebb0732 bf21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
endmodule
